// Logisim project Comp-Arch-Proj-1.circ as structural Verilog: 1 circuit, main circuit main
module main (
);

  wire A1_out, and_1_out, and_2_out, and_3_out, and_4_out, AND_AB_2_out, AND_AB_3_out, AND_AB_4_out,
       AND_AB_out, B1, B1_out, B2, B3, B4, C1_out, Carry_In_out, Clock, D1_out, d_ff_1_qn, d_ff_2_qn,
       d_ff_3_qn, d_ff_4_qn, d_ff_5_q, d_ff_5_qn, d_ff_6_q, d_ff_6_qn, d_ff_7_q, d_ff_7_qn, d_ff_8_q,
       d_ff_8_qn, d_ff_9_qn, d_ff_10_qn, d_ff_11_q, d_ff_11_qn, d_ff_12_q, d_ff_12_qn, multiplexer_1_out,
       multiplexer_2_out, multiplexer_3_out, multiplexer_4_out, or_1_out, or_2_out, or_3_out, or_4_out,
       OR_AB_2_out, OR_AB_3_out, OR_AB_4_out, OR_AB_out, register_1_q, register_2_q, register_3_q,
       register_4_q, Select_1_out, Select_2_out, xor_1_out, xor_2_out, xor_3_out, xor_4_out, xor_5_out,
       xor_6_out, xor_7_out, xor_8_out;
  wire [1:0] register_5_q;

  Button A1 (.out(A1_out));
  Button u_B1 (.out(B1_out));
  Button C1 (.out(C1_out));
  Button D1 (.out(D1_out));
  D_Flip_Flop d_ff_1 (.clk(A1_out), .D(d_ff_5_qn), .Qn(d_ff_1_qn));  // open: Q, preset, en, reset
  D_Flip_Flop d_ff_2 (.clk(B1_out), .D(d_ff_6_qn), .Qn(d_ff_2_qn));  // open: Q, preset, en, reset
  D_Flip_Flop d_ff_3 (.clk(C1_out), .D(d_ff_7_qn), .Qn(d_ff_3_qn));  // open: Q, preset, en, reset
  D_Flip_Flop d_ff_4 (.clk(D1_out), .D(d_ff_8_qn), .Qn(d_ff_4_qn));  // open: Q, preset, en, reset
  D_Flip_Flop d_ff_5 (.clk(A1_out), .D(d_ff_1_qn), .Q(d_ff_5_q), .Qn(d_ff_5_qn));  // open: preset, en, reset
  D_Flip_Flop d_ff_6 (.clk(B1_out), .D(d_ff_2_qn), .Q(d_ff_6_q), .Qn(d_ff_6_qn));  // open: preset, en, reset
  D_Flip_Flop d_ff_7 (.clk(C1_out), .D(d_ff_3_qn), .Q(d_ff_7_q), .Qn(d_ff_7_qn));  // open: preset, en, reset
  D_Flip_Flop d_ff_8 (.clk(D1_out), .D(d_ff_4_qn), .Q(d_ff_8_q), .Qn(d_ff_8_qn));  // open: preset, en, reset
  Register #(.width(1)) register_1 (.D(d_ff_5_q), .Q(register_1_q), .clk(Clock));  // open: en, clr
  Register #(.width(1)) register_2 (.D(d_ff_6_q), .Q(register_2_q), .clk(Clock));  // open: en, clr
  Register #(.width(1)) register_3 (.D(d_ff_7_q), .Q(register_3_q), .clk(Clock));  // open: en, clr
  Register #(.width(1)) register_4 (.D(d_ff_8_q), .Q(register_4_q), .clk(Clock));  // open: en, clr
  Button Carry_In (.out(Carry_In_out));
  xor xor_1 (xor_1_out, register_1_q, B1);
  and and_1 (and_1_out, xor_1_out, Carry_In_out);
  and AND_AB (AND_AB_out, B1, register_1_q);
  or OR_AB (OR_AB_out, B1, register_1_q);
  xor xor_2 (xor_2_out, register_2_q, B2);
  and and_2 (and_2_out, xor_2_out, or_1_out);
  and AND_AB_2 (AND_AB_2_out, B2, register_2_q);
  or OR_AB_2 (OR_AB_2_out, B2, register_2_q);
  xor xor_3 (xor_3_out, register_3_q, B3);
  and and_3 (and_3_out, xor_3_out, or_2_out);
  and AND_AB_3 (AND_AB_3_out, B3, register_3_q);
  or OR_AB_3 (OR_AB_3_out, B3, register_3_q);
  xor xor_4 (xor_4_out, register_4_q, B4);
  and and_4 (and_4_out, xor_4_out, or_3_out);
  and AND_AB_4 (AND_AB_4_out, B4, register_4_q);
  or OR_AB_4 (OR_AB_4_out, B4, register_4_q);
  xor xor_5 (xor_5_out, xor_1_out, Carry_In_out);
  or or_1 (or_1_out, and_1_out, AND_AB_out);
  xor xor_6 (xor_6_out, xor_2_out, or_1_out);
  or or_2 (or_2_out, and_2_out, AND_AB_2_out);
  xor xor_7 (xor_7_out, xor_3_out, or_2_out);
  or or_3 (or_3_out, and_3_out, AND_AB_3_out);
  xor xor_8 (xor_8_out, xor_4_out, or_3_out);
  or or_4 (or_4_out, and_4_out, AND_AB_4_out);
  Button Select_1 (.out(Select_1_out));
  Button Select_2 (.out(Select_2_out));
  LED Carry_Out (.in(or_4_out));
  D_Flip_Flop d_ff_9 (.clk(Select_1_out), .D(d_ff_11_qn), .Qn(d_ff_9_qn));  // open: Q, preset, en, reset
  D_Flip_Flop d_ff_10 (.clk(Select_2_out), .D(d_ff_12_qn), .Qn(d_ff_10_qn));  // open: Q, preset, en, reset
  D_Flip_Flop d_ff_11 (.clk(Select_1_out), .D(d_ff_9_qn), .Q(d_ff_11_q), .Qn(d_ff_11_qn));  // open: preset, en, reset
  D_Flip_Flop d_ff_12 (.clk(Select_2_out), .D(d_ff_10_qn), .Q(d_ff_12_q), .Qn(d_ff_12_qn));  // open: preset, en, reset
  Register #(.width(1)) register_5 (.D(d_ff_11_q), .Q(register_5_q[0]), .clk(Clock));  // open: en, clr
  Register #(.width(1)) register_6 (.D(d_ff_12_q), .Q(register_5_q[1]), .clk(Clock));  // open: en, clr
  Button u_Clock (.out(Clock));
  Multiplexer #(.select(2)) multiplexer_1 (
    .in0(xor_5_out), .in1(AND_AB_out), .in2(OR_AB_out), .in3(1'b0), .out(multiplexer_1_out),
    .sel(register_5_q));  // open: en
  Multiplexer #(.select(2)) multiplexer_2 (
    .in0(xor_6_out), .in1(AND_AB_2_out), .in2(OR_AB_2_out), .in3(1'b0), .out(multiplexer_2_out),
    .sel(register_5_q));  // open: en
  Multiplexer #(.select(2)) multiplexer_3 (
    .in0(xor_7_out), .in1(AND_AB_3_out), .in2(OR_AB_3_out), .in3(1'b0), .out(multiplexer_3_out),
    .sel(register_5_q));  // open: en
  Multiplexer #(.select(2)) multiplexer_4 (
    .in0(xor_8_out), .in1(AND_AB_4_out), .in2(OR_AB_4_out), .in3(1'b0), .out(multiplexer_4_out),
    .sel(register_5_q));  // open: en
  Register #(.width(1)) register_7 (.D(multiplexer_1_out), .Q(B1), .clk(Clock));  // open: en, clr
  Register #(.width(1)) register_8 (.D(multiplexer_2_out), .Q(B2), .clk(Clock));  // open: en, clr
  Register #(.width(1)) register_9 (.D(multiplexer_3_out), .Q(B3), .clk(Clock));  // open: en, clr
  Register #(.width(1)) register_10 (.D(multiplexer_4_out), .Q(B4), .clk(Clock));  // open: en, clr
  LED led_1 (.in(multiplexer_1_out));
  LED led_2 (.in(multiplexer_2_out));
  LED led_3 (.in(multiplexer_3_out));
  LED led_4 (.in(multiplexer_4_out));
endmodule
